// Logisim project alu.circ as structural Verilog: 1 circuit, main circuit arithmetic_logic_unit
module arithmetic_logic_unit (
  input  [7:0] A,
  input  [7:0] B,
  input  [3:0] OP,
  output SIGN,
  output [7:0] Q,
  output Carry
);

  wire adder_2_cout, not_1_out, not_3_out, subtractor_1_bout, subtractor_2_bout;
  wire [7:0] adder_1_out, adder_2_out, and_1_out, controlled_buffer_1_out, controlled_buffer_2_out,
       controlled_inverter_1_out, controlled_inverter_2_out, not_2_out, or_1_out, shifter_1_out,
       shifter_2_out, subtractor_1_out, subtractor_2_out, xor_1_out;

  Shifter shifter_1 (.in(B), .\dist (3'b001), .out(shifter_1_out));
  Shifter #(.shift("lr")) shifter_2 (.in(B), .\dist (3'b001), .out(shifter_2_out));
  Adder adder_1 (.a(B), .b(8'h1), .out(adder_1_out));  // open: cin, cout
  Subtractor subtractor_1 (.a(B), .b(8'h1), .out(subtractor_1_out), .bout(subtractor_1_bout));  // open: bin
  Adder adder_2 (.a(A), .b(B), .out(adder_2_out), .cout(adder_2_cout));  // open: cin
  Subtractor subtractor_2 (.a(A), .b(B), .out(subtractor_2_out), .bout(subtractor_2_bout));  // open: bin
  assign and_1_out = A & B;  // AND_Gate and_1, 8 bits wide
  assign or_1_out = A | B;  // OR_Gate or_1, 8 bits wide
  assign xor_1_out = A ^ B;  // XOR_Gate xor_1, 8 bits wide
  assign controlled_inverter_1_out = subtractor_1_bout ? ~subtractor_1_out : 8'bz;  // Controlled_Inverter controlled_inverter_1
  not not_1 (not_1_out, subtractor_1_bout);
  assign not_2_out = ~A;  // NOT_Gate not_2, 8 bits wide
  assign controlled_inverter_2_out = subtractor_2_bout ? ~subtractor_2_out : 8'bz;  // Controlled_Inverter controlled_inverter_2
  not not_3 (not_3_out, subtractor_2_bout);
  assign controlled_buffer_1_out = not_1_out ? subtractor_1_out : 8'bz;  // Controlled_Buffer controlled_buffer_1
  Adder adder_3 (.a(8'h1), .b(controlled_inverter_1_out), .out(controlled_buffer_1_out));  // open: cin, cout
  assign controlled_buffer_2_out = not_3_out ? subtractor_2_out : 8'bz;  // Controlled_Buffer controlled_buffer_2
  Adder adder_4 (.a(8'h1), .b(controlled_inverter_2_out), .out(controlled_buffer_2_out));  // open: cin, cout
  Multiplexer #(.select(4)) multiplexer_1 (
    .in0(1'b0), .in1(1'b0), .in2(subtractor_2_bout), .in3(1'b0), .in4(1'b0), .in5(1'b0), .in6(1'b0),
    .in7(1'b0), .in8(1'b0), .in9(subtractor_1_bout), .in10(1'b0), .in11(1'b0), .in12(1'b0), .in13(1'b0),
    .in14(1'b0), .in15(1'b0), .out(SIGN), .sel(OP));
  Multiplexer #(.select(4), .width(8)) multiplexer_2 (
    .in1(adder_2_out), .in2(controlled_buffer_2_out), .in3(and_1_out), .in4(or_1_out), .in5(xor_1_out),
    .in6(shifter_1_out), .in7(shifter_2_out), .in8(adder_1_out), .in9(controlled_buffer_1_out),
    .in10(not_2_out), .out(Q), .sel(OP));  // open: in0, in11, in12, in13, in14, in15
  Multiplexer #(.select(4)) multiplexer_3 (
    .in0(1'b0), .in1(adder_2_cout), .in2(1'b0), .in3(1'b0), .in4(1'b0), .in5(1'b0), .in6(B[7]), .in7(B[0]),
    .in8(1'b0), .in9(1'b0), .in10(1'b0), .in11(1'b0), .in12(1'b0), .in13(1'b0), .in14(1'b0), .in15(1'b0),
    .out(Carry), .sel(OP));
endmodule
