// Logisim project flags_register.circ as structural Verilog: 1 circuit, main circuit flags
module flags (
  input  Carry,
  input  Sign,
  input  Zero,
  input  LOAD,
  input  CLK,
  output Carry_out,
  output Sign_out,
  output Zero_out
);

  Register #(.width(3)) register_1 (
    .D({Zero, Sign, Carry}), .en(LOAD), .clk(CLK), .Q({Zero_out, Sign_out, Carry_out}));  // open: clr
endmodule
