// Logisim project full_adders.circ as structural Verilog: 1 circuit, main circuit full_adder
module full_adder (
  input  C_in,
  input  A,
  input  B,
  output C_out,
  output SUM
);

  wire and_1_out, and_2_out, and_3_out, xor_1_out;

  and and_1 (and_1_out, C_in, A);
  and and_2 (and_2_out, C_in, B);
  or or_1 (C_out, and_1_out, and_2_out, and_3_out);
  and and_3 (and_3_out, A, B);
  xor xor_1 (xor_1_out, C_in, A);
  xor xor_2 (SUM, xor_1_out, B);
endmodule
