// Logisim project incrementer_decrementer.circ as structural Verilog: 1 circuit, main circuit inr_dcr
module inr_dcr (
  input  [7:0] D,
  input  INC,
  input  DCR,
  output [7:0] Q,
  output SIGN
);

  wire [7:0] adder_1_out, subtractor_1_out;

  Adder adder_1 (.a(D), .b(8'h1), .out(adder_1_out));  // open: cin, cout
  Subtractor subtractor_1 (.a(D), .b(8'h1), .out(subtractor_1_out), .bout(SIGN));  // open: bin
  assign Q = INC ? adder_1_out : 8'bz;  // Controlled_Buffer controlled_buffer_1
  assign Q = DCR ? subtractor_1_out : 8'bz;  // Controlled_Buffer controlled_buffer_2
endmodule
