// Logisim project program_counter.circ as structural Verilog: 1 circuit, main circuit pc
module pc (
  input  EN,
  input  LOAD,
  input  COUNT,
  input  CLK,
  input  [15:0] D_in,
  output [15:0] Q_out,
  output [15:0] O_out
);

  Counter #(.max('hffff), .width(16)) counter_1 (
    .load(LOAD), .count(COUNT), .clk(CLK), .D(D_in), .Q(O_out));  // open: clr, up, carry
  assign Q_out = EN ? O_out : 16'bz;  // Controlled_Buffer controlled_buffer_1
endmodule
