// Logisim project register_8bits.circ as structural Verilog: 1 circuit, main circuit register_8
module register_8 (
  input  D1,
  input  D2,
  input  D3,
  input  D4,
  input  D5,
  input  D6,
  input  D7,
  input  D8,
  input  LOAD,
  input  CLK,
  input  EN,
  output O1,
  output O2,
  output O3,
  output O4,
  output O5,
  output O6,
  output O7,
  output O8,
  output Q1,
  output Q2,
  output Q3,
  output Q4,
  output Q5,
  output Q6,
  output Q7,
  output Q8
);

  Register register_1 (
    .D({D8, D7, D6, D5, D4, D3, D2, D1}), .en(LOAD), .clk(CLK), .Q({O8, O7, O6, O5, O4, O3, O2, O1}));  // open: clr
  assign {Q8, Q7, Q6, Q5, Q4, Q3, Q2, Q1} = EN ? {O8, O7, O6, O5, O4, O3, O2, O1} : 8'bz;  // Controlled_Buffer controlled_buffer_1
endmodule
