// Logisim project register_z.circ as structural Verilog: 1 circuit, main circuit register_z16bits
module register_z16bits (
  input  D1,
  input  D2,
  input  D3,
  input  D4,
  input  D5,
  input  D6,
  input  D7,
  input  D8,
  input  D9,
  input  D10,
  input  D11,
  input  D12,
  input  D13,
  input  D14,
  input  D15,
  input  D16,
  input  CLK,
  input  LOAD1,
  input  LOAD2,
  input  EN1,
  input  EN2,
  output Q1,
  output Q2,
  output Q3,
  output Q4,
  output Q5,
  output Q6,
  output Q7,
  output Q8,
  output Q9,
  output Q10,
  output Q11,
  output Q12,
  output Q13,
  output Q14,
  output Q15,
  output Q16,
  output O1,
  output O2,
  output O3,
  output O4,
  output O5,
  output O6,
  output O7,
  output O8,
  output O9,
  output O10,
  output O11,
  output O12,
  output O13,
  output O14,
  output O15,
  output O16
);

  Register register_1 (
    .D({D8, D7, D6, D5, D4, D3, D2, D1}), .en(LOAD1), .clk(CLK), .Q({O8, O7, O6, O5, O4, O3, O2, O1}));  // open: clr
  Register register_2 (
    .D({D16, D15, D14, D13, D12, D11, D10, D9}), .en(LOAD2), .clk(CLK),
    .Q({O16, O15, O14, O13, O12, O11, O10, O9}));  // open: clr
  assign {Q8, Q7, Q6, Q5, Q4, Q3, Q2, Q1} = EN1 ? {O8, O7, O6, O5, O4, O3, O2, O1} : 8'bz;  // Controlled_Buffer controlled_buffer_1
  assign {Q16, Q15, Q14, Q13, Q12, Q11, Q10, Q9} = EN2 ? {O16, O15, O14, O13, O12, O11, O10, O9} : 8'bz;  // Controlled_Buffer controlled_buffer_2
endmodule
