// Logisim project ring_counter.circ as structural Verilog: 1 circuit, main circuit ring
module ring (
  input  CLR,
  input  CLK,
  output [3:0] STATE
);

  wire counter_1_carry;

  Counter #(.max('hf), .width(4)) counter_1 (
    .clr(CLR), .up(1'b1), .count(1'b1), .clk(CLK), .carry(counter_1_carry), .Q(STATE));  // open: load, D
endmodule
